# Fritzing sketch 02 - Sensor de temperatura y humedad (saved by Fritzing 0.9.3b)

parts:
  Componente1 = Arduino Uno (Rev3)
  Part1 = KY-015 Temperature & Humidity Sensor Module [package="Breakout board"]

nets:
  N1: Componente1.D2, Part1.S
  5V: Componente1.5V, Part1.Vin
  N2: Componente1.GND, Part1.-

custom parts:
  KY-015 Temperature & Humidity Sensor Module: KY-015 temperature and humidity sensor module, provides a low-latency serial interface to measure humidity and temperature.

// code stored in the sketch: 02-KY015.ino
//www.elegoo.com
//2018.10.25


#include <dht_nonblocking.h>
#define DHT_SENSOR_TYPE DHT_TYPE_11

static const int DHT_SENSOR_PIN = 2;
DHT_nonblocking dht_sensor( DHT_SENSOR_PIN, DHT_SENSOR_TYPE );



/*
 * Initialize the serial port.
 */
void setup( )
{
  Serial.begin( 9600);
}



/*
 * Poll for a measurement, keeping the state machine alive.  Returns
 * true if a measurement is available.
 */
static bool measure_environment( float *temperature, float *humidity )
{
  static unsigned long measurement_timestamp = millis( );

  /* Measure once every four seconds. */
  if( millis( ) - measurement_timestamp > 3000ul )
  {
    if( dht_sensor.measure( temperature, humidity ) == true )
    {
      measurement_timestamp = millis( );
      return( true );
    }
  }

  return( false );
}



/*
 * Main program loop.
 */
void loop( )
{
  float temperature;
  float humidity;

  /* Measure temperature and humidity.  If the functions returns
     true, then a measurement is available. */
  if( measure_environment( &temperature, &humidity ) == true )
  {
    Serial.print( "T = " );
    Serial.print( temperature, 1 );
    Serial.print( " deg. C, H = " );
    Serial.print( humidity, 1 );
    Serial.println( "%" );
  }
}
