# Fritzing sketch 04 - Botón (saved by Fritzing 0.9.3b)

parts:
  Componente1 = Arduino Uno (Rev3)
  Part1 = KY-004 Key Switch Module [package="Breakout board"]

nets:
  N1: Componente1.D3_PWM, Part1.S
  5V: Componente1.5V, Part1.Vin
  N2: Componente1.GND, Part1.-

custom parts:
  KY-004 Key Switch Module: Arduino Key Switch Module Keyes KY-004 is a push button that will output a high signal when pressed.

// code stored in the sketch: 04-KY004.ino
/******************************************
 *Website: www.elegoo.com
 * 
 *Time:2017.12.12
 *
 ******************************************/
int Led = 13; //define LED port
int Shock = 3; //define shock port
int val;//define digital variable val
void  setup()
{
  pinMode(Led, OUTPUT); //define LED as a output port
  pinMode(Shock, INPUT); //define shock sensor as a output port
}
void  loop()
{ val = digitalRead(Shock); //read the value of the digital interface 3 assigned to val
  if (val == HIGH) //when the shock sensor have signal, LED blink
  {
    digitalWrite(Led, LOW);
  }
  else
  {
    digitalWrite(Led, HIGH);
  }
}
