# Fritzing sketch 05 - Interruptores (saved by Fritzing 0.9.3b)

parts:
  Componente1 = Arduino Uno (Rev3)
  Part1 = KY-002 Vibration Switch Module [package="Breakout board"]
  Part2 = KY-021 Mini Magnetic Reed Switch Module [package="Breakout board"]
  Componente2 = Arduino Uno (Rev3)

nets:
  N1: Componente1.D3_PWM, Part2.S
  5V: Componente1.5V, Part2.Vin
  N2: Componente1.GND, Part2.-
  N3: Part1.S, Componente2.D3_PWM
  VIN: Part1.Vin, Componente2.5V
  N4: Part1.-, Componente2.GND

custom parts:
  KY-002 Vibration Switch Module: Arduino Vibration Switch Module KY-002 Keyes allows detection of shock and vibration.
  KY-021 Mini Magnetic Reed Switch Module: KY-021 magnetic reed switch module. A reed switch is a magnetic sensor that is normally open and gets closed when exposed to a magnetic field.

// code stored in the sketch: 05-KY021.ino
/******************************************
  Website: www.elegoo.com

  Time:2017.12.12

 ******************************************/

int Led = 13; //define LED port
int buttonpin = 3; //define switch port
int  val;//define digital variable val
int led_state = 0;

void  setup()
{
  Serial.begin(9600);
  pinMode(Led, OUTPUT); //define LED as a output port
  pinMode(buttonpin, INPUT); //define switch as a output port
  digitalWrite(buttonpin, LOW);
}
void  loop()
{
  val = digitalRead(buttonpin); //read the value of the digital interface 3 assigned to val
  if (val == LOW)
  {
    delay(20);
    led_state = !led_state;
    digitalWrite(Led, led_state);
//    Serial.println("detect shock!");   
  }
}
